# Fritzing sketch GPSSchematic (saved by Fritzing 0.9.3b)
breadboards: 1

parts:
  Part1 = Arduino Nano (Rev3.0)
  Part2 = MicroSD Card Module  # not connected
  GY-NEO6MV3 = SUP500F [package=sup500f]
  Part3 = PowerBoost 500 Charger
  U1 = LIPO-1000mAh [package=lipo-1000]

nets:
  N1: Part1.D0/RX, GY-NEO6MV3.TX-O
  GND: Part1.GND, GY-NEO6MV3.GND, Part3.GND, U1.-
  5V: Part1.5V, GY-NEO6MV3.VCC, Part3.5.0V
  N2: Part3.VBAT_OUT, U1.+

notes:
  GND: Black
  VCC: Red
  TX: Purple
  GND: Black
  VCC: Red
  MISO: Brown
  MOSI: Orange
  SCK: Grey
  CS: Green
